# Fritzing sketch waterbot (saved by Fritzing 0.9.9b)
circuit board: 4.5cm x 3.3cm
breadboards: 1

parts:
  C1 = Ceramic Capacitor [capacitance=0.1µF voltage=35V package="100 mil [THT, multilayer]"]
  Photon = Photon
  Button = screw terminal, 2 pins
  Meter = screw terminal, 2 pins

nets:
  N1: C1.0, Photon.WKP, Meter.pin2
  N2: C1.1, Photon.3V3, Meter.pin1
  N3: Photon.GND, Button.pin2
  N4: Photon.RST, Button.pin1
